# Fritzing sketch schematic (saved by Fritzing 0.9.2b)
circuit board: 5cm x 4cm
perfboards: 1

parts:
  R3 = Resistor [tolerance=±5% resistance=10k package=THT]
  R1 = Resistor [tolerance=±5% resistance=150 package=THT]
  Composant1 = Espruino Pico
  LED1 = LED - 5mm [color="Red (633nm)" package="5 mm [THT]"]
  D1 = Rectifier Diode [part_number=1N4001 package="300 mil [THT]"]
  M1 = DC Motor
  U1 = CNZ1120 [package=cnz1120]
  Q3 = MOSFET-NCHANNEL [package=to220v]
  Q4 = MOSFET-NCHANNEL [package=to220v]
  J1 = female pin header, 2 pins [form="♀ (female)"]
  J2 = female pin header, 2 pins [form="♀ (female)"]
  J3 = female pin header, 2 pins [form="♀ (female)"]
  J4 = female pin header, 2 pins [form="♀ (female)"]
  R2 = Resistor [tolerance=±5% resistance=10k package=THT]

nets:
  N1: R3.Pin_0, Composant1.B3
  N2: R3.Pin_1, Q3.G
  5V: R1.Pin_0, Composant1.Vout, LED1.anode, D1.cathode, M1.pin_1, J3.pin2
  N3: R1.Pin_1, J1.pin1
  N4: Composant1.A5, J3.pin1
  N5: Composant1.B4, R2.Pin_0
  GND: Composant1.GND, Q3.S, Q4.S, J1.pin2
  N6: LED1.cathode, Q4.D
  N7: D1.anode, M1.pin_2, Q3.D
  N8: U1.1, J2.pin2
  N9: U1.2, J2.pin1
  N10: U1.3, J4.pin1
  N11: U1.4, J4.pin2
  N12: Q4.G, R2.Pin_1
