# Fritzing sketch cablage (saved by Fritzing 0.9.2b)
breadboards: 1

parts:
  U1 = Ambient Light Sensor [package=temt6000-sen]
  LED1 = LEDs [package=led10mm]
  R1 = Resistor [tolerance=±5% resistance=220 package=THT]
  R2 = Resistor [tolerance=±5% resistance=33k package=THT]
  part = Espruino Pico
  Q1 = MOSFET-NCHANNEL [package=to220v]
  R3 = Resistor [tolerance=±5% resistance=10k package=THT]
  M1 = DC Motor
  D1 = Rectifier Diode [part_number=1N4001 package="300 mil [THT]"]
  LED2 = LED - 5mm [color="Red (633nm)" package="5 mm [THT]"]

nets:
  5V: U1.C1, LED1.A, part.Vout, M1.pin_1, D1.cathode, LED2.anode
  N1: U1.E1, R2.Pin_1, part.A8
  N2: LED1.C, R1.Pin_1
  GND: R1.Pin_0, R2.Pin_0, part.GND, Q1.S
  N3: part.Vin, M1.pin_2, D1.anode
  N4: part.B1, R3.Pin_0
  N5: Q1.G, R3.Pin_1
  N6: Q1.D, LED2.cathode
