# Fritzing sketch schematic (saved by Fritzing 0.9.2b)
stripboards: 1

parts:
  Composant1 = Espruino Pico
  U1 = mystery part, 8 pins [chip_label=?]
  U2 = mystery part, 8 pins [chip_label=?]
  R1 = Resistor [tolerance=±5% resistance=10k package=THT]
  C1 = Electrolytic Capacitor [capacitance=1µF package="100 mil [THT, electrolytic]"]
  Q1 = Basic FET N-Channel [package="TO220 [THT]"]
  J2 = female pin header, 13 pins [form="♀ (female)"]
  J2_2 = female pin header, 13 pins [form="♀ (female)"]

nets (from the schematic view):
  N1: Composant1.Vin, J2.pin5, J2_2.pin5
  N2: Composant1.B15, U1.pin1
  N3: Composant1.B14, U1.pin2
  N4: Composant1.B13, U1.pin3
  N5: Composant1.B10, J2.pin2, J2_2.pin2
  N6: Composant1.B1, R1.Pin_0
  N7: Composant1.A7, J2.pin4, J2_2.pin4
  N8: Composant1.A6, U1.pin7
  N9: Composant1.A5, U1.pin8
  N10: Composant1.3.3, J2.pin1, J2_2.pin1
  N11: Composant1.Vout, U2.pin8, J2.pin6, J2_2.pin6
  N12: Composant1.GND, U2.pin1, U2.pin7, C1.-, Q1.source, J2.pin7, J2.pin13, J2_2.pin7, J2_2.pin13
  N13: U2.pin3, J2.pin11, J2_2.pin11
  N14: U2.pin4, J2.pin10, J2_2.pin10
  N15: U2.pin5, J2.pin9, J2_2.pin9
  N16: U2.pin6, J2.pin8, J2_2.pin8
  N17: R1.Pin_1, Q1.gate
  N18: Q1.drain, J2.pin3, J2_2.pin3
