# Fritzing sketch cablage espruino pico (saved by Fritzing 0.9.2b)
breadboards: 1

parts:
  Composant1 = Espruino Pico
  M1 = DC Motor
  U1 = CNZ1120 [package=cnz1120]
  R1 = Resistor [tolerance=±5% resistance=150 package=THT]
  D1 = Rectifier Diode [part_number=1N4001 package="300 mil [THT]"]
  Q1 = MOSFET-NCHANNEL [package=sot323]
  R2 = Resistor [tolerance=±5% resistance=10k package=THT]
  LED1 = LED - 5mm [color="Red (633nm)" package="5 mm [THT]"]
  R3 = Resistor [tolerance=±5% resistance=10k package=THT]
  Q2 = MOSFET-NCHANNEL [package=sot323]

nets (from the schematic view):
  N1: Composant1.B10, R3.Pin_0
  N2: Composant1.B1, R2.Pin_0
  N3: Composant1.A8, U1.3
  N4: Composant1.Vout, M1.pin_1, R1.Pin_0, D1.cathode, LED1.anode
  N5: Composant1.GND, U1.2, Q1.S, Q2.S
  N6: M1.pin_2, D1.anode, Q2.D
  N7: U1.1, R1.Pin_1
  N8: Q1.G, R2.Pin_1
  N9: Q1.D, LED1.cathode
  N10: R3.Pin_1, Q2.G
