# Fritzing sketch top_tour (saved by Fritzing 0.9.2b)
breadboards: 1

parts:
  U1 = Ambient Light Sensor [package=temt6000-sen]
  LED1 = LEDs [package=led10mm]
  R1 = Resistor [tolerance=±5% resistance=220 package=THT]
  R2 = Resistor [tolerance=±5% resistance=33k package=THT]

nets:
  5V: U1.C1, LED1.A
  out: U1.E1, R2.Pin_1
  N1: LED1.C, R1.Pin_1
  GND: R1.Pin_0, R2.Pin_0
